# Fritzing sketch wiring (saved by Fritzing 0.9.2b)
breadboards: 1

parts:
  Part1 = Adafruit Feather M0 WINC1500 [part_number="Adafruit #3010"]
  BUTTON1 = Waterproof Pushbutton (green)
  R1 = Resistor [tolerance=±5% resistance=330 package="0402 [SMD]"]

nets:
  N1: Part1.GND, BUTTON1.no_name_yet#5
  N2: Part1.+3V3, BUTTON1.no_name_yet#1, R1.Pin_1
  N3: Part1.D10, BUTTON1.no_name_yet#2
  N4: BUTTON1.no_name_yet#4, R1.Pin_0

custom parts:
  Adafruit Feather M0 WINC1500: This is the Adafruit Feather M0 WiFi w/ATWINC1500 - our take on an 'all-in-one' Arduino-compatible + high speed, reliable WiFi with built in USB and battery charging. Its an Adafruit Feather M0 with a WiFi module, ready to rock! Connect your Feather to the Internet with this fine new FCC-certified WiFi module from Atmel. This 802.11bgn-capable WiFi module is the best new thing for networking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
  Waterproof Pushbutton (green): Waterproof Illuminated Pushbutton (green)
